// Digital circuit register-1bit.dig as structural Verilog
module register_1bit (
  input  D,
  input  C,
  input  en,
  input  rst,
  output Q
);

  Register1 #(.applicationType("IVERILOG"), .CodeFile("C:\\Users\\Berkant\\Desktop\\fpga\\RemedyCpu\\verilog\\reg-1.v")) u_Register1 (
    .D(D), .C(C), .en(en), .rst_n(rst), .Q(Q));
endmodule
