// Digital circuit register-8bit.dig as structural Verilog
module register_8bit (
  input  [7:0] D,
  input  C,
  input  en,
  input  rst,
  output [7:0] Q
);

  Register8 #(.applicationType("IVERILOG"), .CodeFile("C:\\Users\\Berkant\\Desktop\\fpga\\RemedyCpu\\verilog\\reg-8.v")) u_Register8 (
    .D(D), .C(C), .en(en), .rst_n(rst), .Q(Q));
endmodule
